# Fritzing sketch water (saved by Fritzing 1.0.4)
breadboards: 1

parts:
  Chirp!_Soil_Moisture_Sensor1 = Chirp! Soil Moisture Sensor v2.7.3
  A1 = Particle - Photon2
  Relay1 = Relay - 6 pins [package="DIP (Dual Inline) [THT]"]
  OLED_I2C2 = OLED 128x64 I2C Monochrome Display
  Part4 = BME280 Breakout
  WATER_PUMP2 = water pump/motor
  R1 = Resistor [tolerance=±5% resistance=220 package="1206 [SMD]"]
  R2 = Resistor [tolerance=±5% power=0.25W resistance=220 package=THT]
  Q1 = PNP-Transistor [package="SOT-23 [SMD]"]
  J1 = LOAD_CELL [package=1x03]
  Part5 = MQ-131 breakout

nets:
  VDD: Chirp!_Soil_Moisture_Sensor1.Pin_1, A1.Pin_2, A1.Pin_31, Relay1.ON, OLED_I2C2.VDD, J1.B, Part5.VCC
  N1: Chirp!_Soil_Moisture_Sensor1.pin_3, A1.Pin_5
  GND: Chirp!_Soil_Moisture_Sensor1.pin_5, A1.Pin_4, A1.Pin_30, A1.Pin_32, A1.Pin_35, Relay1.GND, OLED_I2C2.GND, WATER_PUMP2.pin_2, R1.Pin_0, R1.Pin_1, Q1.1, J1.W, Part5.GND
  N2: A1.Pin_7, Part5.DO
  N3: A1.Pin_13, Q1.0
  N4: A1.Pin_17, Part4.SCK/SCL
  N5: A1.Pin_18, OLED_I2C2.SCK
  N6: A1.Pin_21, J1.R
  N7: A1.Pin_26, Relay1.VCC
  N8: Relay1.IN, R2.Pin_1, Q1.2
  N9: Relay1.COM, WATER_PUMP2.pin_1

custom parts:
  Particle - Photon2: The Photon 2 is a microcontroller and Wi-Fi networking developed by particle. Features: 802.11a/b/g/n Wi-Fi, 2.4 GHz and 5 GHz Integrated PCB antenna Integrated U.FL connector for external antenna Integrated RF switch BLE 5 using same antenna as Wi-Fi Realtek RTL8721DM MCU ARM Cortex M33 CPU, 200 MHz 2048 KB (2 MB) user application maximum size 3072 KB (3 MB) of RAM available to user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
  Relay - 6 pins: A DIP stand-in part for whatever IC you want. With 6 pins on a 900mil dual inline package (DIP) footprint.
  water pump/motor: WATER PUMP BY ARDUBLOCKTR
  MQ-131 breakout: SKU: 101282
